// Logisim project CPU.circ as structural Verilog: 7 circuits, main circuit Register
module main (
);

  wire clock_1_out, clock_2_out, comparator_1_lt, comparator_2_lt, counter_1_carry, decoder_1_out7,
       decoder_1_out8, decoder_1_out9, decoder_1_out10, Enable_Sub, Halt, Nop, not_1_out, Reset, Sel_B,
       TClock;
  wire [3:0] A, B, Dec, multiplexer_2_out, Op, rom_1_data;
  wire [4:0] counter_1_q, program_counter_1_out_3;
  wire [6:0] adder_1_out, adder_2_out, LSB, MSB;
  wire [7:0] A_MUX, B_MUX, Data, GO_WRITE, multiplexer_4_out, R0, R1, R2, R3, R4, R5, R6, R7, R8;

  Clock clock_1 (.out(clock_1_out));
  Program_Counter program_counter_1 (.TClock(clock_1_out), .Halt(Halt), .out_3(program_counter_1_out_3));
  Register_Bank register_bank_1 (
    .Halt(Halt), .Dec_Output(Dec), .Nop(Nop), .ALU_output(GO_WRITE), .TClock(TClock), .R0(R0), .R1(R1),
    .R2(R2), .R3(R3), .R4(R4), .R5(R5), .R6(R6), .R7(R7), .R8(R8));
  Decoder #(.select(4)) decoder_1 (
    .out7(decoder_1_out7), .out8(decoder_1_out8), .out9(decoder_1_out9), .out10(decoder_1_out10),
    .out11(Nop), .out15(Halt), .sel(Op));  // open: out0, out1, out2, out3, out4, out5, out6, out12, out13, out14, en
  RAM #(.addrWidth(5), .dataWidth(24)) ram_1 (
    .addr(program_counter_1_out_3), .data({Op, Dec, A, B, Data}));  // open: sel, clk, ld, clr
  or or_1 (Enable_Sub, decoder_1_out7, decoder_1_out9);
  or or_2 (Sel_B, decoder_1_out10, decoder_1_out9, decoder_1_out8);
  Multiplexer #(.select(4), .width(8)) multiplexer_1 (
    .in0(R0), .in1(R1), .in2(R2), .in3(R3), .in4(R4), .in5(R5), .in6(R6), .in7(R7), .in8(R8), .out(A_MUX),
    .sel(A));  // open: in9, in10, in11, in12, in13, in14, in15, en
  ALU alu_1 (.Opcode(Op), .A_Input(A_MUX), .B_MUX(B_MUX), .O_p_for_writing(GO_WRITE), .Sub(Enable_Sub));
  Multiplexer #(.width(4)) multiplexer_2 (.in0(B), .in1(4'b1001), .out(multiplexer_2_out), .sel(Sel_B));  // open: en
  Multiplexer #(.select(4), .width(8)) multiplexer_3 (
    .in0(R0), .in1(R1), .in2(R2), .in3(R3), .in4(R4), .in5(R5), .in6(R6), .in7(R7), .in8(R8), .in9(Data),
    .out(B_MUX), .sel(multiplexer_2_out));  // open: in10, in11, in12, in13, in14, in15, en
  TTY #(.rows(33), .cols(1)) tty_1 (.data(MSB), .clk(TClock), .clr(Reset));  // open: we
  TTY #(.rows(33), .cols(1)) tty_2 (.data(LSB), .clk(TClock), .clr(Reset));  // open: we
  Button u_Reset (.out(Reset));
  Counter #(.width(5), .max('h1f)) counter_1 (
    .Q(counter_1_q), .carry(counter_1_carry), .clk(TClock), .clr(Reset));  // open: load, D, count
  Multiplexer #(.select(4), .width(8), .disabled(0), .enable("false")) multiplexer_4 (
    .in0(R0), .in1(R1), .in2(R2), .in3(R3), .in4(R4), .in5(R5), .in6(R6), .in7(R7), .in8(R8),
    .out(multiplexer_4_out), .sel(rom_1_data));  // open: in9, in10, in11, in12, in13, in14, in15
  not not_1 (not_1_out, counter_1_carry);
  Clock clock_2 (.out(clock_2_out));
  and and_1 (TClock, not_1_out, clock_2_out);
  Comparator #(.width(7)) comparator_1 (
    .a(7'b0111001), .b({3'b011, multiplexer_4_out[3:0]}), .lt(comparator_1_lt));  // open: gt, eq
  Comparator #(.width(7)) comparator_2 (
    .a(7'b0111001), .b({3'b011, multiplexer_4_out[7:4]}), .lt(comparator_2_lt));  // open: gt, eq
  ROM #(.addrWidth(5), .dataWidth(4)) rom_1 (.addr(counter_1_q), .data(rom_1_data));  // open: sel
  Adder #(.width(7)) adder_1 (
    .a({3'b011, multiplexer_4_out[3:0]}), .b(7'b0000111), .out(adder_1_out));  // open: cin, cout
  Adder #(.width(7)) adder_2 (
    .a({3'b011, multiplexer_4_out[7:4]}), .b(7'b0000111), .out(adder_2_out));  // open: cin, cout
  Multiplexer #(.width(7), .disabled(0), .enable("false")) multiplexer_5 (
    .in0({3'b011, multiplexer_4_out[3:0]}), .in1(adder_1_out), .out(LSB), .sel(comparator_1_lt));
  Multiplexer #(.width(7), .disabled(0), .enable("false")) multiplexer_6 (
    .in0({3'b011, multiplexer_4_out[7:4]}), .in1(adder_2_out), .out(MSB), .sel(comparator_2_lt));

  // Notes on the sheet:
  //   00
  //   F5
  //   5A
  //   50
  //   FF
  //   0A
  //   4F
  //   F5
  //   EA
  //   7A
  //   9B
  //   65
  //   0F
  //   FF
  //   F5
  //   AA
  //   5A
  //   0A
  //   FA
  //   A5
  //   04
  //   5A
  //   B4
  //   2D
  //   0A
  //   B0
  //   50
  //   0F
  //   00
  //   00
  //   5A
  //   contents of rom_1 (hex, n*v repeats v):
  //   0 0 1 2 3 4 5 6 7 8 2 3 4 5 0 0 1 6 7 8 2 3 4 5 6 6 7 8 2 3 4 4
endmodule

module Register (
  input  Clock,
  input  Enable_from_Dec,
  input  [7:0] ALU_Input,
  output [7:0] Output_to_Reg
);

  D_Flip_Flop d_ff_1 (
    .clk(Clock), .D(ALU_Input[0]), .Q(Output_to_Reg[0]), .en(Enable_from_Dec));  // open: Qn, preset, reset
  D_Flip_Flop d_ff_2 (
    .clk(Clock), .D(ALU_Input[1]), .Q(Output_to_Reg[1]), .en(Enable_from_Dec));  // open: Qn, preset, reset
  D_Flip_Flop d_ff_3 (
    .clk(Clock), .D(ALU_Input[2]), .Q(Output_to_Reg[2]), .en(Enable_from_Dec));  // open: Qn, preset, reset
  D_Flip_Flop d_ff_4 (
    .clk(Clock), .D(ALU_Input[3]), .Q(Output_to_Reg[3]), .en(Enable_from_Dec));  // open: Qn, preset, reset
  D_Flip_Flop d_ff_5 (
    .clk(Clock), .D(ALU_Input[4]), .Q(Output_to_Reg[4]), .en(Enable_from_Dec));  // open: Qn, preset, reset
  D_Flip_Flop d_ff_6 (
    .clk(Clock), .D(ALU_Input[5]), .Q(Output_to_Reg[5]), .en(Enable_from_Dec));  // open: Qn, preset, reset
  D_Flip_Flop d_ff_7 (
    .clk(Clock), .D(ALU_Input[6]), .Q(Output_to_Reg[6]), .en(Enable_from_Dec));  // open: Qn, preset, reset
  D_Flip_Flop d_ff_8 (
    .clk(Clock), .D(ALU_Input[7]), .Q(Output_to_Reg[7]), .en(Enable_from_Dec));  // open: Qn, preset, reset

  // Other names for the same wires on the sheet: Q0 = Output_to_Reg[0]; Q1 = Output_to_Reg[1]; Q2 = Output_to_Reg[2];
  //   Q3 = Output_to_Reg[3]; Q4 = Output_to_Reg[4]; Q5 = Output_to_Reg[5]; Q6 = Output_to_Reg[6];
  //   Q7 = Output_to_Reg[7]
endmodule

// TClock
module Program_Counter (
  input  TClock,
  input  Halt,
  output [4:0] out_3
);

  wire and_1_out, not_1_out, not_2_out, t_ff_1_qn, t_ff_2_qn, t_ff_3_qn, t_ff_4_qn;

  not not_1 (not_1_out, TClock);
  not not_2 (not_2_out, Halt);
  and and_1 (and_1_out, not_1_out, not_2_out);
  T_Flip_Flop t_ff_1 (.clk(and_1_out), .T(1'b1), .Q(out_3[0]), .Qn(t_ff_1_qn));  // open: preset, reset, en
  T_Flip_Flop t_ff_2 (.clk(t_ff_1_qn), .T(1'b1), .Q(out_3[1]), .Qn(t_ff_2_qn));  // open: preset, reset, en
  T_Flip_Flop t_ff_3 (.clk(t_ff_2_qn), .T(1'b1), .Q(out_3[2]), .Qn(t_ff_3_qn));  // open: preset, reset, en
  T_Flip_Flop t_ff_4 (.clk(t_ff_3_qn), .T(1'b1), .Q(out_3[3]), .Qn(t_ff_4_qn));  // open: preset, reset, en
  T_Flip_Flop t_ff_5 (.clk(t_ff_4_qn), .T(1'b1), .Q(out_3[4]));  // open: Qn, preset, reset, en
endmodule

module Register_Bank (
  input  TClock,
  input  Halt,
  input  [3:0] Dec_Output,
  input  Nop,
  input  [7:0] ALU_output,
  output [7:0] R0,
  output [7:0] R1,
  output [7:0] R2,
  output [7:0] R3,
  output [7:0] R4,
  output [7:0] R5,
  output [7:0] R6,
  output [7:0] R7,
  output [7:0] R8
);

  wire decoder_1_out0, decoder_1_out1, decoder_1_out2, decoder_1_out3, decoder_1_out4, decoder_1_out5,
       decoder_1_out6, decoder_1_out7, decoder_1_out8, not_1_out, or_1_out;

  Register register_1 (.ALU_Input(ALU_output), .Clock(TClock), .Enable_from_Dec(decoder_1_out0), .Output_to_Reg(R0));
  Register register_2 (.ALU_Input(ALU_output), .Clock(TClock), .Enable_from_Dec(decoder_1_out1), .Output_to_Reg(R1));
  Register register_3 (.ALU_Input(ALU_output), .Clock(TClock), .Enable_from_Dec(decoder_1_out2), .Output_to_Reg(R2));
  Register register_4 (.ALU_Input(ALU_output), .Clock(TClock), .Enable_from_Dec(decoder_1_out3), .Output_to_Reg(R3));
  Register register_5 (.ALU_Input(ALU_output), .Clock(TClock), .Enable_from_Dec(decoder_1_out4), .Output_to_Reg(R4));
  Register register_6 (.ALU_Input(ALU_output), .Clock(TClock), .Enable_from_Dec(decoder_1_out5), .Output_to_Reg(R5));
  Register register_7 (.ALU_Input(ALU_output), .Clock(TClock), .Enable_from_Dec(decoder_1_out6), .Output_to_Reg(R6));
  Register register_8 (.ALU_Input(ALU_output), .Clock(TClock), .Enable_from_Dec(decoder_1_out7), .Output_to_Reg(R7));
  Register register_9 (.ALU_Input(ALU_output), .Clock(TClock), .Enable_from_Dec(decoder_1_out8), .Output_to_Reg(R8));
  or or_1 (or_1_out, Halt, Nop);
  not not_1 (not_1_out, or_1_out);
  Decoder #(.select(4)) decoder_1 (
    .out0(decoder_1_out0), .out1(decoder_1_out1), .out2(decoder_1_out2), .out3(decoder_1_out3),
    .out4(decoder_1_out4), .out5(decoder_1_out5), .out6(decoder_1_out6), .out7(decoder_1_out7),
    .out8(decoder_1_out8), .sel(Dec_Output), .en(not_1_out));  // open: out9, out10, out11, out12, out13, out14, out15
endmodule

module _1BitCLU (
  input  G3,
  input  P3,
  input  P0,
  input  P1,
  input  P2,
  input  G0,
  input  G1,
  input  G2,
  input  CIN,
  output C1,
  output C2,
  output C3,
  output C4
);

  wire and_1_out, and_2_out, CinP0_out, CinP0P1_out, CinP0P1P2_out, P1G0_out, P2G1_out, P2P1G0_out, P3G2_out,
       P3P2P1P0C0_out;

  and and_1 (and_1_out, P3, P2, G1);
  and P3P2P1P0C0 (P3P2P1P0C0_out, P3, P2, P1, P0, CIN);
  and and_2 (and_2_out, P3, P2, P1, G0);
  and CinP0 (CinP0_out, P0, CIN);
  and CinP0P1 (CinP0P1_out, P0, CIN, P1);
  and P1G0 (P1G0_out, G0, P1);
  and CinP0P1P2 (CinP0P1P2_out, CIN, P0, P1, P2);
  and P2P1G0 (P2P1G0_out, P2, P1, G0);
  and P2G1 (P2G1_out, P2, G1);
  and P3G2 (P3G2_out, G2, P3);
  or or_1 (C1, CinP0_out, G0);
  or or_2 (C2, CinP0P1_out, P1G0_out, G1);
  or or_3 (C3, CinP0P1P2_out, P2P1G0_out, P2G1_out, G2);
  or or_4 (C4, P3G2_out, P3P2P1P0C0_out, G3, and_1_out, and_2_out);

  // Other names for the same wires on the sheet: C0 = CIN

  // Notes on the sheet:
  //   P3
  //   G3
  //   P0
  //   P1
  //   P2
  //   G0
  //   G1
  //   G2
  //   CIN
endmodule

// ALU
module _1BitALU (
  input  A,
  input  Prev,
  input  Next,
  input  B,
  input  C,
  input  Sub,
  input  [3:0] in_7,
  output O_p,
  output Generate,
  output Propogate
);

  wire Gen, multiplexer_1_out, not_1_out, not_2_out, Prop, xor_1_out, xor_2_out;

  not not_1 (not_1_out, B);
  Multiplexer multiplexer_1 (.in0(B), .in1(not_1_out), .out(multiplexer_1_out), .sel(Sub));  // open: en
  and A0B0 (Gen, A, B);
  or or_1 (Prop, A, B);
  not not_2 (not_2_out, A);
  xor xor_1 (xor_1_out, A, multiplexer_1_out);
  xor xor_2 (xor_2_out, xor_1_out, C);
  and and_1 (Generate, multiplexer_1_out, A);
  or or_2 (Propogate, A, multiplexer_1_out);
  Multiplexer #(.select(4), .enable("false")) multiplexer_2 (
    .in0(Gen), .in1(Prop), .in2(not_2_out), .in3(xor_2_out), .in4(A), .in5(Prev), .in6(Next),
    .in7(xor_2_out), .in8(xor_2_out), .in9(xor_2_out), .in10(B), .out(O_p), .sel(in_7));  // open: in11, in12, in13, in14, in15

  // Other names for the same wires on the sheet: Opcode[3:0] = in_7
endmodule

module ALU (
  input  [3:0] Opcode,
  input  [7:0] A_Input,
  input  Sub,
  input  [7:0] B_MUX,
  output [7:0] O_p_for_writing
);

  wire C1, C2, C3, C4, C5, C6, C7, C8, G0, G1, G2, G3, G4, G5, G6, G7, P0, P1, P2, P3, P4, P5, P6, P7;

  _1BitALU _0 (
    .A(A_Input[0]), .Prev(1'b0), .Next(A_Input[1]), .B(B_MUX[0]), .C(Sub), .in_7(Opcode),
    .O_p(O_p_for_writing[0]), .Generate(G0), .Propogate(P0), .Sub(Sub));
  _1BitALU u_1bitalu_1 (
    .A(A_Input[4]), .Prev(A_Input[3]), .Next(A_Input[5]), .B(B_MUX[4]), .C(C4), .in_7(Opcode),
    .O_p(O_p_for_writing[4]), .Generate(G4), .Propogate(P4), .Sub(Sub));
  _1BitCLU CLU (
    .C4(C4), .G3(G3), .P3(P3), .P0(P0), .P1(P1), .P2(P2), .G0(G0), .G1(G1), .G2(G2), .CIN(Sub), .C1(C1),
    .C2(C2), .C3(C3));
  _1BitALU _1 (
    .A(A_Input[1]), .Prev(A_Input[0]), .Next(A_Input[2]), .B(B_MUX[1]), .C(C1), .in_7(Opcode),
    .O_p(O_p_for_writing[1]), .Generate(G1), .Propogate(P1), .Sub(Sub));
  _1BitALU u_1bitalu_2 (
    .A(A_Input[5]), .Prev(A_Input[4]), .Next(A_Input[6]), .B(B_MUX[5]), .C(C5), .in_7(Opcode),
    .O_p(O_p_for_writing[5]), .Generate(G5), .Propogate(P5), .Sub(Sub));
  _1BitCLU CLU_2 (
    .C4(C8), .G3(G7), .P3(P7), .P0(P4), .P1(P5), .P2(P6), .G0(G4), .G1(G5), .G2(G6), .CIN(C4), .C1(C5),
    .C2(C6), .C3(C7));
  _1BitALU _2 (
    .A(A_Input[2]), .Prev(A_Input[1]), .Next(A_Input[3]), .B(B_MUX[2]), .C(C2), .in_7(Opcode),
    .O_p(O_p_for_writing[2]), .Generate(G2), .Propogate(P2), .Sub(Sub));
  _1BitALU u_1bitalu_3 (
    .A(A_Input[6]), .Prev(A_Input[5]), .Next(A_Input[7]), .B(B_MUX[6]), .C(C6), .in_7(Opcode),
    .O_p(O_p_for_writing[6]), .Generate(G6), .Propogate(P6), .Sub(Sub));
  _1BitALU _3 (
    .A(A_Input[3]), .Prev(A_Input[2]), .Next(A_Input[4]), .B(B_MUX[3]), .C(C3), .in_7(Opcode),
    .O_p(O_p_for_writing[3]), .Generate(G3), .Propogate(P3), .Sub(Sub));
  _1BitALU u_1bitalu_4 (
    .A(A_Input[7]), .Prev(A_Input[6]), .Next(1'b0), .B(B_MUX[7]), .C(C7), .in_7(Opcode),
    .O_p(O_p_for_writing[7]), .Generate(G7), .Propogate(P7), .Sub(Sub));

  // Other names for the same wires on the sheet: A0 = A_Input[0]; A1 = A_Input[1]; A2 = A_Input[2]; A3 = A_Input[3];
  //   A4 = A_Input[4]; A5 = A_Input[5]; A6 = A_Input[6]; A7 = A_Input[7]; B0 = B_MUX[0]; B1 = B_MUX[1]; B2 = B_MUX[2];
  //   B3 = B_MUX[3]; B4 = B_MUX[4]; B5 = B_MUX[5]; B6 = B_MUX[6]; B7 = B_MUX[7]; O0 = O_p_for_writing[0];
  //   O1 = O_p_for_writing[1]; O2 = O_p_for_writing[2]; O3 = O_p_for_writing[3]; O4 = O_p_for_writing[4];
  //   O5 = O_p_for_writing[5]; O6 = O_p_for_writing[6]; O7 = O_p_for_writing[7]; Op[3:0] = Opcode
endmodule
